# Fritzing sketch Blink (saved by Fritzing 0.9.3b)
circuit board: 2.2564cm x 6.12811cm
breadboards: 1

parts:
  R2 = Resistor [tolerance=±5% resistance=220 package=THT]
  R1 = Resistor [tolerance=±5% resistance=220 package=THT]
  LED1 = LED - 5mm [color="Yellow (595nm)" package="5 mm [THT]"]
  LED2 = LED - 5mm [color="Green (560nm)" package="5 mm [THT]"]
  Arduno_Nano = Arduino Nano (Rev3.0)

nets:
  N1: R2.Pin_0, Arduno_Nano.D3
  N2: R2.Pin_1, LED2.anode
  N3: R1.Pin_0, Arduno_Nano.D2
  N4: R1.Pin_1, LED1.anode
  N5: LED1.cathode, LED2.cathode, Arduno_Nano.GND

// code stored in the sketch: Blink__transcripted.ino
#include <ArduinoSTL.h>
#include <vector>
using namespace std;

void Blink(){
    /*feedback and shift regs. declarations */
    
    /* END feedback and shift regs declarations */
    bool wireUID_424_ = true;
    bool wireUID_740_ = true;
    long wireUID_705_ = 3;
    long wireUID_652_ = 2;
    pinMode(wireUID_652_,wireUID_740_?OUTPUT:INPUT);
    pinMode(wireUID_705_,wireUID_740_?OUTPUT:INPUT);
    /***** BEGIN WhileLoop ********/
    vector< bool > feedbackNode_615;
    bool feedbackNodeInitBool_615 = true;
    
    bool wireUID_430_ = false; //LoopEndRef.
    int iteratorUID_289 = 0; //loop iterator
    do{
     //shift register init and get front value
        /*feedback and shift regs. declarations */
        
        /* END feedback and shift regs declarations */
        bool wireUID_317_;
        bool wireUID_642_;
        long wireUID_1157_ = 2;
        long wireUID_921_ = 3;
        long wireUID_426_ = 220;
        if (feedbackNodeInitBool_615){
            feedbackNode_615.push_back(wireUID_424_);
            feedbackNodeInitBool_615 = false;
        }
        wireUID_642_ = feedbackNode_615.front(); feedbackNode_615.erase(feedbackNode_615.begin());
        delay(wireUID_426_);
        wireUID_317_ = !wireUID_642_;
        digitalWrite(wireUID_921_,wireUID_642_?HIGH:LOW);
        /* Don't know how to translate class "Generic ->GObject ->Node": "" */
        digitalWrite(wireUID_1157_,wireUID_317_?HIGH:LOW);
        feedbackNode_615.push_back(wireUID_317_);
        
        
         //C code
        
         //output assgn.
        iteratorUID_289++; //iterator increment
    }while(!wireUID_430_); //negation because in LabVIEW it is when stop (oposite)
    
    /****** END WhileLoop */
    
    
    
}

void setup(){
    Blink();
}
void loop(){
}
